// Logisim project 10th Digit.circ as structural Verilog: 1 circuit, main circuit 10th Digit
module _10th_Digit (
  input  in_1,
  input  in_2,
  input  in_3,
  input  in_4,
  output _3,
  output _4,
  output _7,
  output _6,
  output _5,
  output _2,
  output _1
);

  wire and_1_out, and_2_out, and_3_out, and_4_out, and_5_out, and_6_out, and_7_out, and_8_out, and_9_out,
       and_10_out, and_11_out, and_12_out, and_13_out, not_1_out, not_2_out, not_3_out, not_4_out;

  not not_1 (not_1_out, in_1);
  not not_2 (not_2_out, in_2);
  not not_3 (not_3_out, in_3);
  not not_4 (not_4_out, in_4);
  and and_1 (and_1_out, in_2, in_4);
  and and_2 (and_2_out, not_2_out, not_4_out);
  and and_3 (and_3_out, in_3, in_4);
  and and_4 (and_4_out, not_3_out, not_4_out);
  and and_5 (and_5_out, not_4_out, in_3);
  and and_6 (and_6_out, not_1_out, not_2_out);
  and and_7 (and_7_out, in_1, not_4_out);
  and and_8 (and_8_out, in_2, not_3_out);
  and and_9 (and_9_out, in_2, not_4_out);
  and and_10 (and_10_out, in_3, not_2_out);
  and and_11 (and_11_out, in_3, and_6_out);
  and and_12 (and_12_out, and_6_out, not_4_out);
  and and_13 (and_13_out, and_1_out, not_3_out);
  or or_1 (_3, in_1, in_3, and_1_out, and_2_out);
  or or_2 (_4, not_2_out, and_3_out, and_4_out);
  or or_3 (_7, in_1, not_3_out, in_2, in_4);
  or or_4 (_6, in_1, and_5_out, and_11_out, and_12_out, and_13_out);
  or or_5 (_5, and_5_out, and_12_out, and_7_out);
  or or_6 (_2, in_1, and_4_out, and_8_out, and_9_out);
  or or_7 (_1, in_1, and_5_out, and_8_out, and_10_out);

  // Notes on the sheet:
  //   10th Digit Generator
endmodule
