// Logisim project Even & Odd Counter Final Design.circ as structural Verilog: 1 circuit, main circuit VIP
module VIP (
  input  _1___ODD_Counter
);

  wire and_1_out, and_2_out, and_3_out, and_4_out, and_5_out, and_6_out, clock_1_out, j_k_ff_1_q, j_k_ff_2_q,
       j_k_ff_3_q, j_k_ff_4_q, j_k_ff_5_q, j_k_ff_6_q, j_k_ff_7_q, n10th_digit_1__1, n10th_digit_1__2,
       n10th_digit_1__3, n10th_digit_1__4, n10th_digit_1__5, n10th_digit_1__6, n10th_digit_1__7, not_1_out,
       or_1_out, or_2_out, unit_digit_1__1, unit_digit_1__2, unit_digit_1__3, unit_digit_1__4,
       unit_digit_1__5, unit_digit_1__6, unit_digit_1__7;

  Clock clock_1 (.out(clock_1_out));
  J_K_Flip_Flop j_k_ff_1 (
    .J(1'b1), .clk(clock_1_out), .K(1'b1), .Q(j_k_ff_1_q), .reset(and_4_out));  // open: Qn, preset, en
  not not_1 (not_1_out, and_1_out);
  J_K_Flip_Flop j_k_ff_2 (
    .J(not_1_out), .clk(not_1_out), .K(not_1_out), .Q(j_k_ff_2_q), .reset(and_6_out));  // open: Qn, preset, en
  J_K_Flip_Flop j_k_ff_3 (
    .J(j_k_ff_1_q), .clk(clock_1_out), .K(j_k_ff_1_q), .Q(j_k_ff_3_q), .reset(and_4_out));  // open: Qn, preset, en
  and and_1 (and_1_out, or_2_out, or_1_out);
  and and_2 (and_2_out, j_k_ff_2_q, j_k_ff_4_q);
  J_K_Flip_Flop j_k_ff_4 (
    .J(j_k_ff_2_q), .clk(not_1_out), .K(j_k_ff_2_q), .Q(j_k_ff_4_q), .reset(and_6_out));  // open: Qn, preset, en
  and and_3 (and_3_out, j_k_ff_1_q, j_k_ff_3_q);
  J_K_Flip_Flop j_k_ff_5 (
    .J(and_2_out), .clk(not_1_out), .K(and_2_out), .Q(j_k_ff_5_q), .reset(and_6_out));  // open: Qn, preset, en
  J_K_Flip_Flop j_k_ff_6 (
    .J(and_3_out), .clk(clock_1_out), .K(and_3_out), .Q(j_k_ff_6_q), .reset(and_4_out));  // open: Qn, preset, en
  and and_4 (and_4_out, j_k_ff_6_q, j_k_ff_1_q);
  and and_5 (and_5_out, and_2_out, j_k_ff_5_q);
  J_K_Flip_Flop j_k_ff_7 (
    .J(and_5_out), .clk(not_1_out), .K(and_5_out), .Q(j_k_ff_7_q), .reset(and_6_out));  // open: Qn, preset, en
  and and_6 (and_6_out, j_k_ff_7_q, j_k_ff_4_q);
  or or_1 (or_1_out, j_k_ff_6_q, j_k_ff_3_q, j_k_ff_1_q);
  or or_2 (or_2_out, j_k_ff_6_q, j_k_ff_1_q, j_k_ff_3_q, _1___ODD_Counter);
  _10th_Digit u_10th_digit_1 (
    .in_1(j_k_ff_7_q), .in_2(j_k_ff_5_q), .in_3(j_k_ff_4_q), .in_4(j_k_ff_2_q), ._3(n10th_digit_1__3),
    ._4(n10th_digit_1__4), ._7(n10th_digit_1__7), ._6(n10th_digit_1__6), ._5(n10th_digit_1__5),
    ._2(n10th_digit_1__2), ._1(n10th_digit_1__1));
  _7_Segment_Display u_7_segment_display_1 (
    .g(n10th_digit_1__1), .f(n10th_digit_1__2), .a(n10th_digit_1__3), .b(n10th_digit_1__4),
    .e(n10th_digit_1__5), .d(n10th_digit_1__6), .c(n10th_digit_1__7));  // open: dp
  Unit_Digit unit_digit_1 (
    .in_1(j_k_ff_6_q), .in_2(j_k_ff_3_q), .in_3(j_k_ff_1_q), .in_4(_1___ODD_Counter), ._3(unit_digit_1__3),
    ._4(unit_digit_1__4), ._7(unit_digit_1__7), ._6(unit_digit_1__6), ._5(unit_digit_1__5),
    ._2(unit_digit_1__2), ._1(unit_digit_1__1));
  _7_Segment_Display u_7_segment_display_2 (
    .g(unit_digit_1__1), .f(unit_digit_1__2), .a(unit_digit_1__3), .b(unit_digit_1__4), .e(unit_digit_1__5),
    .d(unit_digit_1__6), .c(unit_digit_1__7));  // open: dp

  // Notes on the sheet:
  //   Input 1
  //   Clock
  //   0 : EVEN Counter
  //   Even & Odd Counter using J-K Flipflop 
  //   Even & Odd Counter using J-K Flipflop 
  //   Fundamental of Digital Electronics
  //   Reference
  //   Book : Digital Logic and Computer Design
  //   Author : M. MORRIS MANO
  //   Project Engineers
  //   Chaitanya Patel (11BCE069)
  //   Darshil Patel     (11BCE070)
  //   Vivek Patel       (11BCE073)
  //   Computer Engineering Department
  //   Institute of Technology
  //   Nirma University
endmodule
